# Fritzing sketch GreenhouseControler (saved by Fritzing 0.9.2b)
breadboards: 1

parts:
  Part2 = Arduino Nano (Rev3.0) (ICSP)
  Part3 = Arduino Ethernet Shield (Rev3)  # not connected
  Part5 = Breadboard Power Supply Board SMD
  Part6 = DeadOn RTC - DS3234 Breakout
  DHT1 = DHT11 Humitidy and Temperature Sensor
  LED1 = RGB LED (com. cathode, rbg) [color="Red (633nm)" package="5 mm [THT]"]  # not connected
  o1 = Module display OLED I2C 128x64 SSD1306 [package=THT]
  X2 = USB Connectors [package=usb-a-s-nosilk]
  Q1 = TRANSISTOR_NPN [package=to-92]
  R1 = Resistor [tolerance=±5% resistance=2.2k package="2512 [SMD]"]

nets:
  GND: Part2.GND, Part5.GND, Part6.GND, DHT1.GND, o1.GND, Q1.E
  N1: Part2.D4, R1.Pin_1
  N2: Part2.D5, Part6.MOSI
  N3: Part2.D6, Part6.MISO
  N4: Part2.D7, Part6.SCLK
  N5: Part2.D8, DHT1.DATA
  N6: Part2.D9, Part6.SS
  VCC: Part2.VIN, Part5.VCC, Part6.VCC, DHT1.VDD, o1.VCC, X2.VBUS
  N7: Part2.A5, o1.SCL
  N8: Part2.A4, o1.SDA
  N9: X2.GND, Q1.C
  N10: Q1.B, R1.Pin_0

custom parts:
  DHT11 Humitidy and Temperature Sensor: DHT11 Humidity and Temperature Sensor
  Module display OLED I2C 128x64 SSD1306: Ecran OLED I2C SSD163 de 128x64 avec connexion I2C

// code stored in the sketch: GreenhouseControler.ino
/*
Greenhousecontroller.ino
Code written by Shai Perednik shaiss@gmail.com
First coding 7/16/2015
Using Arduino Nano
 */


//Define Pins
int DHpin = 2; //Temp  & Humidity Senosor DHT11 or DHT12
byte dat[5]; //Values in DHTXX

//helper funcation to get  data from DHTXX
byte read_data()
{
  byte data;
  for (int i = 0; i < 8; i++)
  {
    if (digitalRead(DHpin) == LOW)
    {
      while (digitalRead(DHpin) == LOW);
      delayMicroseconds(30);
      if (digitalRead(DHpin) == HIGH)
        data |= (1 << (7 - i));
      while (digitalRead(DHpin) == HIGH);
    }
  }
  return data;
}

//funtion to 
void start_test()
{
  digitalWrite(DHpin, LOW);//turn the sensor pin off
  delay(30);
  digitalWrite(DHpin, HIGH); //turn the sensor pin on
  delayMicroseconds(40);
  pinMode(DHpin, INPUT); //make the sensor pin an Input

  while (digitalRead(DHpin) == HIGH);
  delayMicroseconds(80); 
  if (digitalRead(DHpin) == LOW);
  delayMicroseconds(80);
  for (int i = 0; i < 4; i++)
    dat[i] = read_data();
  pinMode(DHpin, OUTPUT);
  digitalWrite(DHpin, HIGH);
}

//First run setup here
void setup()
{
  Serial.begin(9600);
  pinMode(DHpin, OUTPUT);
}

//Loop that runs forever
void loop()
{
  start_test();
  Serial.print("Current humdity = ");
  Serial.print(dat[0], DEC);
  Serial.print('.');
  Serial.print(dat[1], DEC);
  Serial.println('%');
  Serial.print("Current temperature = ");
  Serial.print(dat[2], DEC);
  Serial.print('.');
  Serial.print(dat[3], DEC);
  Serial.println('C');
  delay(700);
}
